// Logisim project LittleDrop.circ as structural Verilog: 10 circuits, main circuit main
module main (
  input  in_1
);

  wire clock_1_out, d_ff_1_q;

  Clock clock_1 (.out(clock_1_out));
  D_FF d_ff_1 (.D(in_1), .Clock(clock_1_out), .Q(d_ff_1_q));  // open: Q_prime
  LED led_1 (.in(d_ff_1_q));
endmodule

module HA (
  input  a,
  input  b,
  output S,
  output Cout
);

  xor xor_1 (S, a, b);
  and and_1 (Cout, a, b);
endmodule

module FA (
  input  a,
  input  b,
  input  Cin,
  output S,
  output Cout
);

  wire and_1_out, and_2_out, xor_1_out;

  xor xor_1 (xor_1_out, a, b);
  and and_1 (and_1_out, xor_1_out, Cin);
  and and_2 (and_2_out, a, b);
  xor xor_2 (S, xor_1_out, Cin);
  or or_1 (Cout, and_1_out, and_2_out);
endmodule

module NOR_FF (
  input  Reset,
  input  Set,
  output Q,
  output Q_prime
);

  nor nor_1 (Q, Reset, Q_prime);
  nor nor_2 (Q_prime, Q, Set);
endmodule

module NAND_FF (
  input  Reset,
  input  Set,
  output Q,
  output Q_prime
);

  nand nand_1 (Q, Reset, Q_prime);
  nand nand_2 (Q_prime, Q, Set);
endmodule

module D_FF (
  input  D,
  input  Clock,
  output Q,
  output Q_prime
);

  wire nand_1_out, nand_2_out, not_1_out;

  not not_1 (not_1_out, D);
  nand nand_1 (nand_1_out, D, Clock);
  nand nand_2 (nand_2_out, Clock, not_1_out);
  nand nand_3 (Q, nand_1_out, Q_prime);
  nand nand_4 (Q_prime, nand_2_out, Q);
endmodule

module J_K_FF (
  input  J,
  input  Clock,
  input  K,
  output Q,
  output Q_prime
);

  wire and_1_out, and_2_out;

  and and_1 (and_1_out, Q, J, Clock);
  and and_2 (and_2_out, Clock, K, Q_prime);
  nor nor_1 (Q, and_1_out, Q_prime);
  nor nor_2 (Q_prime, Q, and_2_out);
endmodule

module T_FF (
  input  T,
  input  Clock,
  output Q,
  output Q_prime
);

  wire and_1_out, and_2_out;

  and and_1 (and_1_out, Q, T, Clock);
  and and_2 (and_2_out, Clock, T, Q_prime);
  nor nor_1 (Q, and_1_out, Q_prime);
  nor nor_2 (Q_prime, Q, and_2_out);
endmodule

module Transition (
  input  Clock,
  output Clock_prime
);

  wire not_1_out;

  not not_1 (not_1_out, Clock);
  and and_1 (Clock_prime, not_1_out, Clock);
endmodule

module Register (
  input  D3,
  input  D2,
  input  D1,
  input  D0,
  input  Clock,
  output D0_prime,
  output D1_prime,
  output D2_prime,
  output D3_prime,
  output I0,
  output I1,
  output I2,
  output I3
);

  D_FF d_ff_1 (.Clock(D0), .Q_prime(D0_prime));  // open: D, Q
  D_FF d_ff_2 (.Clock(D1), .Q_prime(D1_prime));  // open: D, Q
  D_FF d_ff_3 (.D(D2), .Clock(D2), .Q_prime(D2_prime));  // open: Q
  D_FF d_ff_4 (.D(D3), .Clock(D3), .Q_prime(D3_prime));  // open: Q
endmodule
